// Logisim project main.circ as structural Verilog: 7 circuits, main circuit main
module main (
  input  Hold
);

  wire \bit , cdm16e_1_p2, cdm16e_1_p5, cdm16e_1_p6, cdm16e_1_p7, cdm16e_1_p8, cdm16e_1_p9, cdm16e_1_p10,
       cdm16e_1_p11, cdm16e_1_p12, cdm16e_1_p13, cl, mem, not_1_out, r_w, screen_mem_1_clock_out,
       screen_mem_2_clock_out, screen_mem_3_clock_out, screen_mem_4_clock_out;
  wire [15:0] addr, cdm16e_1_p18, cdm16e_1_p19, data, np1, np2, np3, r1, screen_mem_1__14,
       screen_mem_1__14_2, screen_mem_1_addr_pass, screen_mem_1_data_pass, screen_mem_1_next_pos,
       screen_mem_1_str0, screen_mem_1_str0_2, screen_mem_1_str1, screen_mem_1_str1_2, screen_mem_1_str2,
       screen_mem_1_str2_2, screen_mem_1_str3, screen_mem_1_str3_2, screen_mem_1_str4, screen_mem_1_str4_2,
       screen_mem_1_str5, screen_mem_1_str5_2, screen_mem_1_str6, screen_mem_1_str6_2, screen_mem_1_str7,
       screen_mem_1_str7_2, screen_mem_1_str8, screen_mem_1_str8_2, screen_mem_1_str9, screen_mem_1_str9_2,
       screen_mem_1_str10, screen_mem_1_str10_2, screen_mem_1_str11, screen_mem_1_str11_2,
       screen_mem_1_str12, screen_mem_1_str12_2, screen_mem_1_str13, screen_mem_1_str13_2,
       screen_mem_1_str15, screen_mem_1_str15_2, screen_mem_2__14, screen_mem_2__14_2,
       screen_mem_2_addr_pass, screen_mem_2_data_pass, screen_mem_2_next_pos, screen_mem_2_str0,
       screen_mem_2_str0_2, screen_mem_2_str1, screen_mem_2_str1_2, screen_mem_2_str2, screen_mem_2_str2_2,
       screen_mem_2_str3, screen_mem_2_str3_2, screen_mem_2_str4, screen_mem_2_str4_2, screen_mem_2_str5,
       screen_mem_2_str5_2, screen_mem_2_str6, screen_mem_2_str6_2, screen_mem_2_str7, screen_mem_2_str7_2,
       screen_mem_2_str8, screen_mem_2_str8_2, screen_mem_2_str9, screen_mem_2_str9_2, screen_mem_2_str10,
       screen_mem_2_str10_2, screen_mem_2_str11, screen_mem_2_str11_2, screen_mem_2_str12,
       screen_mem_2_str12_2, screen_mem_2_str13, screen_mem_2_str13_2, screen_mem_2_str15,
       screen_mem_2_str15_2, screen_mem_3__14, screen_mem_3__14_2, screen_mem_3_addr_pass,
       screen_mem_3_data_pass, screen_mem_3_next_pos, screen_mem_3_str0, screen_mem_3_str0_2,
       screen_mem_3_str1, screen_mem_3_str1_2, screen_mem_3_str2, screen_mem_3_str2_2, screen_mem_3_str3,
       screen_mem_3_str3_2, screen_mem_3_str4, screen_mem_3_str4_2, screen_mem_3_str5, screen_mem_3_str5_2,
       screen_mem_3_str6, screen_mem_3_str6_2, screen_mem_3_str7, screen_mem_3_str7_2, screen_mem_3_str8,
       screen_mem_3_str8_2, screen_mem_3_str9, screen_mem_3_str9_2, screen_mem_3_str10, screen_mem_3_str10_2,
       screen_mem_3_str11, screen_mem_3_str11_2, screen_mem_3_str12, screen_mem_3_str12_2,
       screen_mem_3_str13, screen_mem_3_str13_2, screen_mem_3_str15, screen_mem_3_str15_2, screen_mem_4__14,
       screen_mem_4__14_2, screen_mem_4_addr_pass, screen_mem_4_data_pass, screen_mem_4_next_pos,
       screen_mem_4_str0, screen_mem_4_str0_2, screen_mem_4_str1, screen_mem_4_str1_2, screen_mem_4_str2,
       screen_mem_4_str2_2, screen_mem_4_str3, screen_mem_4_str3_2, screen_mem_4_str4, screen_mem_4_str4_2,
       screen_mem_4_str5, screen_mem_4_str5_2, screen_mem_4_str6, screen_mem_4_str6_2, screen_mem_4_str7,
       screen_mem_4_str7_2, screen_mem_4_str8, screen_mem_4_str8_2, screen_mem_4_str9, screen_mem_4_str9_2,
       screen_mem_4_str10, screen_mem_4_str10_2, screen_mem_4_str11, screen_mem_4_str11_2,
       screen_mem_4_str12, screen_mem_4_str12_2, screen_mem_4_str13, screen_mem_4_str13_2,
       screen_mem_4_str15, screen_mem_4_str15_2, screen_mem_5__14, screen_mem_5__14_2, screen_mem_5_str0,
       screen_mem_5_str0_2, screen_mem_5_str1, screen_mem_5_str1_2, screen_mem_5_str2, screen_mem_5_str2_2,
       screen_mem_5_str3, screen_mem_5_str3_2, screen_mem_5_str4, screen_mem_5_str4_2, screen_mem_5_str5,
       screen_mem_5_str5_2, screen_mem_5_str6, screen_mem_5_str6_2, screen_mem_5_str7, screen_mem_5_str7_2,
       screen_mem_5_str8, screen_mem_5_str8_2, screen_mem_5_str9, screen_mem_5_str9_2, screen_mem_5_str10,
       screen_mem_5_str10_2, screen_mem_5_str11, screen_mem_5_str11_2, screen_mem_5_str12,
       screen_mem_5_str12_2, screen_mem_5_str13, screen_mem_5_str13_2, screen_mem_5_str15,
       screen_mem_5_str15_2, screen_mem_6__14, screen_mem_6__14_2, screen_mem_6_str0, screen_mem_6_str0_2,
       screen_mem_6_str1, screen_mem_6_str1_2, screen_mem_6_str2, screen_mem_6_str2_2, screen_mem_6_str3,
       screen_mem_6_str3_2, screen_mem_6_str4, screen_mem_6_str4_2, screen_mem_6_str5, screen_mem_6_str5_2,
       screen_mem_6_str6, screen_mem_6_str6_2, screen_mem_6_str7, screen_mem_6_str7_2, screen_mem_6_str8,
       screen_mem_6_str8_2, screen_mem_6_str9, screen_mem_6_str9_2, screen_mem_6_str10, screen_mem_6_str10_2,
       screen_mem_6_str11, screen_mem_6_str11_2, screen_mem_6_str12, screen_mem_6_str12_2,
       screen_mem_6_str13, screen_mem_6_str13_2, screen_mem_6_str15, screen_mem_6_str15_2, screen_mem_7__14,
       screen_mem_7__14_2, screen_mem_7_str0, screen_mem_7_str0_2, screen_mem_7_str1, screen_mem_7_str1_2,
       screen_mem_7_str2, screen_mem_7_str2_2, screen_mem_7_str3, screen_mem_7_str3_2, screen_mem_7_str4,
       screen_mem_7_str4_2, screen_mem_7_str5, screen_mem_7_str5_2, screen_mem_7_str6, screen_mem_7_str6_2,
       screen_mem_7_str7, screen_mem_7_str7_2, screen_mem_7_str8, screen_mem_7_str8_2, screen_mem_7_str9,
       screen_mem_7_str9_2, screen_mem_7_str10, screen_mem_7_str10_2, screen_mem_7_str11,
       screen_mem_7_str11_2, screen_mem_7_str12, screen_mem_7_str12_2, screen_mem_7_str13,
       screen_mem_7_str13_2, screen_mem_7_str15, screen_mem_7_str15_2, screen_mem_8__14, screen_mem_8__14_2,
       screen_mem_8_str0, screen_mem_8_str0_2, screen_mem_8_str1, screen_mem_8_str1_2, screen_mem_8_str2,
       screen_mem_8_str2_2, screen_mem_8_str3, screen_mem_8_str3_2, screen_mem_8_str4, screen_mem_8_str4_2,
       screen_mem_8_str5, screen_mem_8_str5_2, screen_mem_8_str6, screen_mem_8_str6_2, screen_mem_8_str7,
       screen_mem_8_str7_2, screen_mem_8_str8, screen_mem_8_str8_2, screen_mem_8_str9, screen_mem_8_str9_2,
       screen_mem_8_str10, screen_mem_8_str10_2, screen_mem_8_str11, screen_mem_8_str11_2,
       screen_mem_8_str12, screen_mem_8_str12_2, screen_mem_8_str13, screen_mem_8_str13_2,
       screen_mem_8_str15, screen_mem_8_str15_2;

  // Probe on cdm16e_1_p2
  // Probe on cdm16e_1_p2
  // Probe on cdm16e_1_p2
  Clock clock_1 (.out(cl));
  // Probe on r1
  // Probe on r1
  // Probe on r1
  // Probe on cdm16e_1_p5
  // Probe on cdm16e_1_p5
  // Probe on cdm16e_1_p5
  // cdm16e cdm16e_1: pin names not known; wires that end beside it: Hold, cdm16e_1_p2, r1, cl, cdm16e_1_p5, cdm16e_1_p6, cdm16e_1_p7, cdm16e_1_p8, cdm16e_1_p9, cdm16e_1_p10, cdm16e_1_p11, cdm16e_1_p12, cdm16e_1_p13, mem, r_w, \bit , addr, cdm16e_1_p18, cdm16e_1_p19
  // Probe on data
  // Probe on data
  // Probe on data
  // Probe on data
  // Probe on addr
  // Probe on addr
  // Probe on addr
  // Probe on addr
  // Probe on cdm16e_1_p6
  // Probe on cdm16e_1_p6
  // Probe on cdm16e_1_p6
  assign data = not_1_out ? cdm16e_1_p18 : 16'bz;  // Controlled_Buffer controlled_buffer_1
  not not_1 (not_1_out, r_w);
  assign cdm16e_1_p19 = r_w ? data : 16'bz;  // Controlled_Buffer controlled_buffer_2
  // Probe on cdm16e_1_p7
  // Probe on cdm16e_1_p7
  // Probe on cdm16e_1_p7
  // Probe on cdm16e_1_p8
  // Probe on cdm16e_1_p8
  // Probe on cdm16e_1_p8
  DotMatrix #(.matrixcols(32), .matrixrows(16)) dotmatrix_1 (
    .col0(screen_mem_1_str0), .col1(screen_mem_1_str1), .col2(screen_mem_1_str2), .col3(screen_mem_1_str3),
    .col4(screen_mem_1_str4), .col5(screen_mem_1_str5), .col6(screen_mem_1_str6), .col7(screen_mem_1_str7),
    .col8(screen_mem_1_str8), .col9(screen_mem_1_str9), .col10(screen_mem_1_str10),
    .col11(screen_mem_1_str11), .col12(screen_mem_1_str12), .col13(screen_mem_1_str13),
    .col14(screen_mem_1__14), .col15(screen_mem_1_str15), .col16(screen_mem_1_str0_2),
    .col17(screen_mem_1_str1_2), .col18(screen_mem_1_str2_2), .col19(screen_mem_1_str3_2),
    .col20(screen_mem_1_str4_2), .col21(screen_mem_1_str5_2), .col22(screen_mem_1_str6_2),
    .col23(screen_mem_1_str7_2), .col24(screen_mem_1_str8_2), .col25(screen_mem_1_str9_2),
    .col26(screen_mem_1_str10_2), .col27(screen_mem_1_str11_2), .col28(screen_mem_1_str12_2),
    .col29(screen_mem_1_str13_2), .col30(screen_mem_1__14_2), .col31(screen_mem_1_str15_2));
  DotMatrix #(.matrixcols(32), .matrixrows(16)) dotmatrix_2 (
    .col0(screen_mem_2_str0), .col1(screen_mem_2_str1), .col2(screen_mem_2_str2), .col3(screen_mem_2_str3),
    .col4(screen_mem_2_str4), .col5(screen_mem_2_str5), .col6(screen_mem_2_str6), .col7(screen_mem_2_str7),
    .col8(screen_mem_2_str8), .col9(screen_mem_2_str9), .col10(screen_mem_2_str10),
    .col11(screen_mem_2_str11), .col12(screen_mem_2_str12), .col13(screen_mem_2_str13),
    .col14(screen_mem_2__14), .col15(screen_mem_2_str15), .col16(screen_mem_2_str0_2),
    .col17(screen_mem_2_str1_2), .col18(screen_mem_2_str2_2), .col19(screen_mem_2_str3_2),
    .col20(screen_mem_2_str4_2), .col21(screen_mem_2_str5_2), .col22(screen_mem_2_str6_2),
    .col23(screen_mem_2_str7_2), .col24(screen_mem_2_str8_2), .col25(screen_mem_2_str9_2),
    .col26(screen_mem_2_str10_2), .col27(screen_mem_2_str11_2), .col28(screen_mem_2_str12_2),
    .col29(screen_mem_2_str13_2), .col30(screen_mem_2__14_2), .col31(screen_mem_2_str15_2));
  DotMatrix #(.matrixcols(32), .matrixrows(16)) dotmatrix_3 (
    .col0(screen_mem_3_str0), .col1(screen_mem_3_str1), .col2(screen_mem_3_str2), .col3(screen_mem_3_str3),
    .col4(screen_mem_3_str4), .col5(screen_mem_3_str5), .col6(screen_mem_3_str6), .col7(screen_mem_3_str7),
    .col8(screen_mem_3_str8), .col9(screen_mem_3_str9), .col10(screen_mem_3_str10),
    .col11(screen_mem_3_str11), .col12(screen_mem_3_str12), .col13(screen_mem_3_str13),
    .col14(screen_mem_3__14), .col15(screen_mem_3_str15), .col16(screen_mem_3_str0_2),
    .col17(screen_mem_3_str1_2), .col18(screen_mem_3_str2_2), .col19(screen_mem_3_str3_2),
    .col20(screen_mem_3_str4_2), .col21(screen_mem_3_str5_2), .col22(screen_mem_3_str6_2),
    .col23(screen_mem_3_str7_2), .col24(screen_mem_3_str8_2), .col25(screen_mem_3_str9_2),
    .col26(screen_mem_3_str10_2), .col27(screen_mem_3_str11_2), .col28(screen_mem_3_str12_2),
    .col29(screen_mem_3_str13_2), .col30(screen_mem_3__14_2), .col31(screen_mem_3_str15_2));
  DotMatrix #(.matrixcols(32), .matrixrows(16)) dotmatrix_4 (
    .col0(screen_mem_4_str0), .col1(screen_mem_4_str1), .col2(screen_mem_4_str2), .col3(screen_mem_4_str3),
    .col4(screen_mem_4_str4), .col5(screen_mem_4_str5), .col6(screen_mem_4_str6), .col7(screen_mem_4_str7),
    .col8(screen_mem_4_str8), .col9(screen_mem_4_str9), .col10(screen_mem_4_str10),
    .col11(screen_mem_4_str11), .col12(screen_mem_4_str12), .col13(screen_mem_4_str13),
    .col14(screen_mem_4__14), .col15(screen_mem_4_str15), .col16(screen_mem_4_str0_2),
    .col17(screen_mem_4_str1_2), .col18(screen_mem_4_str2_2), .col19(screen_mem_4_str3_2),
    .col20(screen_mem_4_str4_2), .col21(screen_mem_4_str5_2), .col22(screen_mem_4_str6_2),
    .col23(screen_mem_4_str7_2), .col24(screen_mem_4_str8_2), .col25(screen_mem_4_str9_2),
    .col26(screen_mem_4_str10_2), .col27(screen_mem_4_str11_2), .col28(screen_mem_4_str12_2),
    .col29(screen_mem_4_str13_2), .col30(screen_mem_4__14_2), .col31(screen_mem_4_str15_2));
  // Probe on cdm16e_1_p9
  // Probe on cdm16e_1_p9
  // Probe on cdm16e_1_p9
  // Probe on cdm16e_1_p10
  // Probe on cdm16e_1_p10
  // Probe on cdm16e_1_p10
  // RAM ram_1: pin names not known; wires that end beside it: addr, \bit , mem, cl, r_w, data
  screen_mem screen_mem_1 (
    .clock(cl), .data(data), .addr(addr), .start_pos(r1), .str0(screen_mem_1_str0), .str1(screen_mem_1_str1),
    .str2(screen_mem_1_str2), .str3(screen_mem_1_str3), .str4(screen_mem_1_str4), .str5(screen_mem_1_str5),
    .str6(screen_mem_1_str6), .str7(screen_mem_1_str7), .str8(screen_mem_1_str8), .str9(screen_mem_1_str9),
    .str10(screen_mem_1_str10), .str11(screen_mem_1_str11), .str12(screen_mem_1_str12),
    .str13(screen_mem_1_str13), ._14(screen_mem_1__14), .str15(screen_mem_1_str15),
    .str0_2(screen_mem_1_str0_2), .str1_2(screen_mem_1_str1_2), .str2_2(screen_mem_1_str2_2),
    .str3_2(screen_mem_1_str3_2), .str4_2(screen_mem_1_str4_2), .str5_2(screen_mem_1_str5_2),
    .str6_2(screen_mem_1_str6_2), .str7_2(screen_mem_1_str7_2), .str8_2(screen_mem_1_str8_2),
    .str9_2(screen_mem_1_str9_2), .str10_2(screen_mem_1_str10_2), .str11_2(screen_mem_1_str11_2),
    .str12_2(screen_mem_1_str12_2), .str13_2(screen_mem_1_str13_2), ._14_2(screen_mem_1__14_2),
    .str15_2(screen_mem_1_str15_2), .next_pos(screen_mem_1_next_pos), .clock_out(screen_mem_1_clock_out),
    .data_pass(screen_mem_1_data_pass), .addr_pass(screen_mem_1_addr_pass));
  screen_mem screen_mem_2 (
    .clock(cl), .data(data), .addr(addr), .start_pos(np1), .str0(screen_mem_2_str0),
    .str1(screen_mem_2_str1), .str2(screen_mem_2_str2), .str3(screen_mem_2_str3), .str4(screen_mem_2_str4),
    .str5(screen_mem_2_str5), .str6(screen_mem_2_str6), .str7(screen_mem_2_str7), .str8(screen_mem_2_str8),
    .str9(screen_mem_2_str9), .str10(screen_mem_2_str10), .str11(screen_mem_2_str11),
    .str12(screen_mem_2_str12), .str13(screen_mem_2_str13), ._14(screen_mem_2__14),
    .str15(screen_mem_2_str15), .str0_2(screen_mem_2_str0_2), .str1_2(screen_mem_2_str1_2),
    .str2_2(screen_mem_2_str2_2), .str3_2(screen_mem_2_str3_2), .str4_2(screen_mem_2_str4_2),
    .str5_2(screen_mem_2_str5_2), .str6_2(screen_mem_2_str6_2), .str7_2(screen_mem_2_str7_2),
    .str8_2(screen_mem_2_str8_2), .str9_2(screen_mem_2_str9_2), .str10_2(screen_mem_2_str10_2),
    .str11_2(screen_mem_2_str11_2), .str12_2(screen_mem_2_str12_2), .str13_2(screen_mem_2_str13_2),
    ._14_2(screen_mem_2__14_2), .str15_2(screen_mem_2_str15_2), .next_pos(screen_mem_2_next_pos),
    .clock_out(screen_mem_2_clock_out), .data_pass(screen_mem_2_data_pass), .addr_pass(screen_mem_2_addr_pass));
  screen_mem screen_mem_3 (
    .clock(cl), .data(data), .addr(addr), .start_pos(np2), .str0(screen_mem_3_str0),
    .str1(screen_mem_3_str1), .str2(screen_mem_3_str2), .str3(screen_mem_3_str3), .str4(screen_mem_3_str4),
    .str5(screen_mem_3_str5), .str6(screen_mem_3_str6), .str7(screen_mem_3_str7), .str8(screen_mem_3_str8),
    .str9(screen_mem_3_str9), .str10(screen_mem_3_str10), .str11(screen_mem_3_str11),
    .str12(screen_mem_3_str12), .str13(screen_mem_3_str13), ._14(screen_mem_3__14),
    .str15(screen_mem_3_str15), .str0_2(screen_mem_3_str0_2), .str1_2(screen_mem_3_str1_2),
    .str2_2(screen_mem_3_str2_2), .str3_2(screen_mem_3_str3_2), .str4_2(screen_mem_3_str4_2),
    .str5_2(screen_mem_3_str5_2), .str6_2(screen_mem_3_str6_2), .str7_2(screen_mem_3_str7_2),
    .str8_2(screen_mem_3_str8_2), .str9_2(screen_mem_3_str9_2), .str10_2(screen_mem_3_str10_2),
    .str11_2(screen_mem_3_str11_2), .str12_2(screen_mem_3_str12_2), .str13_2(screen_mem_3_str13_2),
    ._14_2(screen_mem_3__14_2), .str15_2(screen_mem_3_str15_2), .next_pos(screen_mem_3_next_pos),
    .clock_out(screen_mem_3_clock_out), .data_pass(screen_mem_3_data_pass), .addr_pass(screen_mem_3_addr_pass));
  screen_mem screen_mem_4 (
    .clock(cl), .data(data), .addr(addr), .start_pos(np3), .str0(screen_mem_4_str0),
    .str1(screen_mem_4_str1), .str2(screen_mem_4_str2), .str3(screen_mem_4_str3), .str4(screen_mem_4_str4),
    .str5(screen_mem_4_str5), .str6(screen_mem_4_str6), .str7(screen_mem_4_str7), .str8(screen_mem_4_str8),
    .str9(screen_mem_4_str9), .str10(screen_mem_4_str10), .str11(screen_mem_4_str11),
    .str12(screen_mem_4_str12), .str13(screen_mem_4_str13), ._14(screen_mem_4__14),
    .str15(screen_mem_4_str15), .str0_2(screen_mem_4_str0_2), .str1_2(screen_mem_4_str1_2),
    .str2_2(screen_mem_4_str2_2), .str3_2(screen_mem_4_str3_2), .str4_2(screen_mem_4_str4_2),
    .str5_2(screen_mem_4_str5_2), .str6_2(screen_mem_4_str6_2), .str7_2(screen_mem_4_str7_2),
    .str8_2(screen_mem_4_str8_2), .str9_2(screen_mem_4_str9_2), .str10_2(screen_mem_4_str10_2),
    .str11_2(screen_mem_4_str11_2), .str12_2(screen_mem_4_str12_2), .str13_2(screen_mem_4_str13_2),
    ._14_2(screen_mem_4__14_2), .str15_2(screen_mem_4_str15_2), .next_pos(screen_mem_4_next_pos),
    .clock_out(screen_mem_4_clock_out), .data_pass(screen_mem_4_data_pass), .addr_pass(screen_mem_4_addr_pass));
  // Probe on cdm16e_1_p11
  // Probe on cdm16e_1_p11
  // Probe on cdm16e_1_p11
  // Probe on cdm16e_1_p12
  // Probe on cdm16e_1_p12
  // Probe on cdm16e_1_p12
  // Debugger debugger_1: pin names not known
  DotMatrix #(.matrixcols(32), .matrixrows(16)) dotmatrix_5 (
    .col0(screen_mem_5_str0), .col1(screen_mem_5_str1), .col2(screen_mem_5_str2), .col3(screen_mem_5_str3),
    .col4(screen_mem_5_str4), .col5(screen_mem_5_str5), .col6(screen_mem_5_str6), .col7(screen_mem_5_str7),
    .col8(screen_mem_5_str8), .col9(screen_mem_5_str9), .col10(screen_mem_5_str10),
    .col11(screen_mem_5_str11), .col12(screen_mem_5_str12), .col13(screen_mem_5_str13),
    .col14(screen_mem_5__14), .col15(screen_mem_5_str15), .col16(screen_mem_5_str0_2),
    .col17(screen_mem_5_str1_2), .col18(screen_mem_5_str2_2), .col19(screen_mem_5_str3_2),
    .col20(screen_mem_5_str4_2), .col21(screen_mem_5_str5_2), .col22(screen_mem_5_str6_2),
    .col23(screen_mem_5_str7_2), .col24(screen_mem_5_str8_2), .col25(screen_mem_5_str9_2),
    .col26(screen_mem_5_str10_2), .col27(screen_mem_5_str11_2), .col28(screen_mem_5_str12_2),
    .col29(screen_mem_5_str13_2), .col30(screen_mem_5__14_2), .col31(screen_mem_5_str15_2));
  DotMatrix #(.matrixcols(32), .matrixrows(16)) dotmatrix_6 (
    .col0(screen_mem_6_str0), .col1(screen_mem_6_str1), .col2(screen_mem_6_str2), .col3(screen_mem_6_str3),
    .col4(screen_mem_6_str4), .col5(screen_mem_6_str5), .col6(screen_mem_6_str6), .col7(screen_mem_6_str7),
    .col8(screen_mem_6_str8), .col9(screen_mem_6_str9), .col10(screen_mem_6_str10),
    .col11(screen_mem_6_str11), .col12(screen_mem_6_str12), .col13(screen_mem_6_str13),
    .col14(screen_mem_6__14), .col15(screen_mem_6_str15), .col16(screen_mem_6_str0_2),
    .col17(screen_mem_6_str1_2), .col18(screen_mem_6_str2_2), .col19(screen_mem_6_str3_2),
    .col20(screen_mem_6_str4_2), .col21(screen_mem_6_str5_2), .col22(screen_mem_6_str6_2),
    .col23(screen_mem_6_str7_2), .col24(screen_mem_6_str8_2), .col25(screen_mem_6_str9_2),
    .col26(screen_mem_6_str10_2), .col27(screen_mem_6_str11_2), .col28(screen_mem_6_str12_2),
    .col29(screen_mem_6_str13_2), .col30(screen_mem_6__14_2), .col31(screen_mem_6_str15_2));
  DotMatrix #(.matrixcols(32), .matrixrows(16)) dotmatrix_7 (
    .col0(screen_mem_7_str0), .col1(screen_mem_7_str1), .col2(screen_mem_7_str2), .col3(screen_mem_7_str3),
    .col4(screen_mem_7_str4), .col5(screen_mem_7_str5), .col6(screen_mem_7_str6), .col7(screen_mem_7_str7),
    .col8(screen_mem_7_str8), .col9(screen_mem_7_str9), .col10(screen_mem_7_str10),
    .col11(screen_mem_7_str11), .col12(screen_mem_7_str12), .col13(screen_mem_7_str13),
    .col14(screen_mem_7__14), .col15(screen_mem_7_str15), .col16(screen_mem_7_str0_2),
    .col17(screen_mem_7_str1_2), .col18(screen_mem_7_str2_2), .col19(screen_mem_7_str3_2),
    .col20(screen_mem_7_str4_2), .col21(screen_mem_7_str5_2), .col22(screen_mem_7_str6_2),
    .col23(screen_mem_7_str7_2), .col24(screen_mem_7_str8_2), .col25(screen_mem_7_str9_2),
    .col26(screen_mem_7_str10_2), .col27(screen_mem_7_str11_2), .col28(screen_mem_7_str12_2),
    .col29(screen_mem_7_str13_2), .col30(screen_mem_7__14_2), .col31(screen_mem_7_str15_2));
  DotMatrix #(.matrixcols(32), .matrixrows(16)) dotmatrix_8 (
    .col0(screen_mem_8_str0), .col1(screen_mem_8_str1), .col2(screen_mem_8_str2), .col3(screen_mem_8_str3),
    .col4(screen_mem_8_str4), .col5(screen_mem_8_str5), .col6(screen_mem_8_str6), .col7(screen_mem_8_str7),
    .col8(screen_mem_8_str8), .col9(screen_mem_8_str9), .col10(screen_mem_8_str10),
    .col11(screen_mem_8_str11), .col12(screen_mem_8_str12), .col13(screen_mem_8_str13),
    .col14(screen_mem_8__14), .col15(screen_mem_8_str15), .col16(screen_mem_8_str0_2),
    .col17(screen_mem_8_str1_2), .col18(screen_mem_8_str2_2), .col19(screen_mem_8_str3_2),
    .col20(screen_mem_8_str4_2), .col21(screen_mem_8_str5_2), .col22(screen_mem_8_str6_2),
    .col23(screen_mem_8_str7_2), .col24(screen_mem_8_str8_2), .col25(screen_mem_8_str9_2),
    .col26(screen_mem_8_str10_2), .col27(screen_mem_8_str11_2), .col28(screen_mem_8_str12_2),
    .col29(screen_mem_8_str13_2), .col30(screen_mem_8__14_2), .col31(screen_mem_8_str15_2));
  // Probe on cdm16e_1_p13
  // Probe on cdm16e_1_p13
  // Probe on cdm16e_1_p13
  screen_mem screen_mem_5 (
    .clock(screen_mem_1_clock_out), .data(screen_mem_1_data_pass), .addr(screen_mem_1_addr_pass),
    .start_pos(screen_mem_1_next_pos), .str0(screen_mem_5_str0), .str1(screen_mem_5_str1),
    .str2(screen_mem_5_str2), .str3(screen_mem_5_str3), .str4(screen_mem_5_str4), .str5(screen_mem_5_str5),
    .str6(screen_mem_5_str6), .str7(screen_mem_5_str7), .str8(screen_mem_5_str8), .str9(screen_mem_5_str9),
    .str10(screen_mem_5_str10), .str11(screen_mem_5_str11), .str12(screen_mem_5_str12),
    .str13(screen_mem_5_str13), ._14(screen_mem_5__14), .str15(screen_mem_5_str15),
    .str0_2(screen_mem_5_str0_2), .str1_2(screen_mem_5_str1_2), .str2_2(screen_mem_5_str2_2),
    .str3_2(screen_mem_5_str3_2), .str4_2(screen_mem_5_str4_2), .str5_2(screen_mem_5_str5_2),
    .str6_2(screen_mem_5_str6_2), .str7_2(screen_mem_5_str7_2), .str8_2(screen_mem_5_str8_2),
    .str9_2(screen_mem_5_str9_2), .str10_2(screen_mem_5_str10_2), .str11_2(screen_mem_5_str11_2),
    .str12_2(screen_mem_5_str12_2), .str13_2(screen_mem_5_str13_2), ._14_2(screen_mem_5__14_2),
    .str15_2(screen_mem_5_str15_2), .next_pos(np1));  // open: clock_out, data_pass, addr_pass
  screen_mem screen_mem_6 (
    .clock(screen_mem_2_clock_out), .data(screen_mem_2_data_pass), .addr(screen_mem_2_addr_pass),
    .start_pos(screen_mem_2_next_pos), .str0(screen_mem_6_str0), .str1(screen_mem_6_str1),
    .str2(screen_mem_6_str2), .str3(screen_mem_6_str3), .str4(screen_mem_6_str4), .str5(screen_mem_6_str5),
    .str6(screen_mem_6_str6), .str7(screen_mem_6_str7), .str8(screen_mem_6_str8), .str9(screen_mem_6_str9),
    .str10(screen_mem_6_str10), .str11(screen_mem_6_str11), .str12(screen_mem_6_str12),
    .str13(screen_mem_6_str13), ._14(screen_mem_6__14), .str15(screen_mem_6_str15),
    .str0_2(screen_mem_6_str0_2), .str1_2(screen_mem_6_str1_2), .str2_2(screen_mem_6_str2_2),
    .str3_2(screen_mem_6_str3_2), .str4_2(screen_mem_6_str4_2), .str5_2(screen_mem_6_str5_2),
    .str6_2(screen_mem_6_str6_2), .str7_2(screen_mem_6_str7_2), .str8_2(screen_mem_6_str8_2),
    .str9_2(screen_mem_6_str9_2), .str10_2(screen_mem_6_str10_2), .str11_2(screen_mem_6_str11_2),
    .str12_2(screen_mem_6_str12_2), .str13_2(screen_mem_6_str13_2), ._14_2(screen_mem_6__14_2),
    .str15_2(screen_mem_6_str15_2), .next_pos(np2));  // open: clock_out, data_pass, addr_pass
  screen_mem screen_mem_7 (
    .clock(screen_mem_3_clock_out), .data(screen_mem_3_data_pass), .addr(screen_mem_3_addr_pass),
    .start_pos(screen_mem_3_next_pos), .str0(screen_mem_7_str0), .str1(screen_mem_7_str1),
    .str2(screen_mem_7_str2), .str3(screen_mem_7_str3), .str4(screen_mem_7_str4), .str5(screen_mem_7_str5),
    .str6(screen_mem_7_str6), .str7(screen_mem_7_str7), .str8(screen_mem_7_str8), .str9(screen_mem_7_str9),
    .str10(screen_mem_7_str10), .str11(screen_mem_7_str11), .str12(screen_mem_7_str12),
    .str13(screen_mem_7_str13), ._14(screen_mem_7__14), .str15(screen_mem_7_str15),
    .str0_2(screen_mem_7_str0_2), .str1_2(screen_mem_7_str1_2), .str2_2(screen_mem_7_str2_2),
    .str3_2(screen_mem_7_str3_2), .str4_2(screen_mem_7_str4_2), .str5_2(screen_mem_7_str5_2),
    .str6_2(screen_mem_7_str6_2), .str7_2(screen_mem_7_str7_2), .str8_2(screen_mem_7_str8_2),
    .str9_2(screen_mem_7_str9_2), .str10_2(screen_mem_7_str10_2), .str11_2(screen_mem_7_str11_2),
    .str12_2(screen_mem_7_str12_2), .str13_2(screen_mem_7_str13_2), ._14_2(screen_mem_7__14_2),
    .str15_2(screen_mem_7_str15_2), .next_pos(np3));  // open: clock_out, data_pass, addr_pass
  screen_mem screen_mem_8 (
    .clock(screen_mem_4_clock_out), .data(screen_mem_4_data_pass), .addr(screen_mem_4_addr_pass),
    .start_pos(screen_mem_4_next_pos), .str0(screen_mem_8_str0), .str1(screen_mem_8_str1),
    .str2(screen_mem_8_str2), .str3(screen_mem_8_str3), .str4(screen_mem_8_str4), .str5(screen_mem_8_str5),
    .str6(screen_mem_8_str6), .str7(screen_mem_8_str7), .str8(screen_mem_8_str8), .str9(screen_mem_8_str9),
    .str10(screen_mem_8_str10), .str11(screen_mem_8_str11), .str12(screen_mem_8_str12),
    .str13(screen_mem_8_str13), ._14(screen_mem_8__14), .str15(screen_mem_8_str15),
    .str0_2(screen_mem_8_str0_2), .str1_2(screen_mem_8_str1_2), .str2_2(screen_mem_8_str2_2),
    .str3_2(screen_mem_8_str3_2), .str4_2(screen_mem_8_str4_2), .str5_2(screen_mem_8_str5_2),
    .str6_2(screen_mem_8_str6_2), .str7_2(screen_mem_8_str7_2), .str8_2(screen_mem_8_str8_2),
    .str9_2(screen_mem_8_str9_2), .str10_2(screen_mem_8_str10_2), .str11_2(screen_mem_8_str11_2),
    .str12_2(screen_mem_8_str12_2), .str13_2(screen_mem_8_str13_2), ._14_2(screen_mem_8__14_2),
    .str15_2(screen_mem_8_str15_2));  // open: next_pos, clock_out, data_pass, addr_pass
endmodule

module data_sel (
  input  [15:0] out,
  input  r_w,
  input  [15:0] in,
  output [15:0] data
);

  wire not_1_out;

  assign data = not_1_out ? out : 16'bz;  // Controlled_Buffer controlled_buffer_1
  not not_1 (not_1_out, r_w);
  assign in = r_w ? data : 16'bz;  // Controlled_Buffer controlled_buffer_2
endmodule

// MEM BANK
module gpu_str_mem (
  input  [15:0] data,
  input  [15:0] addr,
  input  clock,
  input  [15:0] pos,
  output [15:0] str,
  output [15:0] pos_next
);

  wire comparator_1_eq;
  wire [15:0] multiplexer_1_out;

  Comparator #(.width(16), .mode("unsigned")) comparator_1 (.a(addr), .b(pos), .eq(comparator_1_eq));  // open: gt, lt
  Adder #(.width(16)) adder_1 (.a(pos), .b(16'h2), .out(pos_next));  // open: cin, cout
  Multiplexer #(.width(16)) multiplexer_1 (
    .in0(str), .in1(data), .out(multiplexer_1_out), .sel(comparator_1_eq));  // open: en
  Register #(.width(16)) register_1 (.D(multiplexer_1_out), .Q(str), .clk(clock));  // open: en, clr
endmodule

// SCREEN MEMORY
module screen_mem (
  input  [15:0] data,
  input  [15:0] addr,
  input  clock,
  input  [15:0] start_pos,
  output [15:0] str0,
  output [15:0] str1,
  output [15:0] str2,
  output [15:0] str3,
  output [15:0] str4,
  output [15:0] str5,
  output [15:0] str6,
  output [15:0] str7,
  output [15:0] str8,
  output [15:0] str9,
  output [15:0] str10,
  output [15:0] str11,
  output [15:0] str12,
  output [15:0] str13,
  output [15:0] _14,
  output [15:0] str15,
  output [15:0] str0_2,
  output [15:0] str1_2,
  output [15:0] str2_2,
  output [15:0] str3_2,
  output [15:0] str4_2,
  output [15:0] str5_2,
  output [15:0] str6_2,
  output [15:0] str7_2,
  output [15:0] str8_2,
  output [15:0] str9_2,
  output [15:0] str10_2,
  output [15:0] str11_2,
  output [15:0] str12_2,
  output [15:0] str13_2,
  output [15:0] _14_2,
  output [15:0] str15_2,
  output [15:0] data_pass,
  output clock_out,
  output [15:0] addr_pass,
  output [15:0] next_pos
);

  wire [15:0] gpu_compute_module_1_next_gen0, gpu_compute_module_1_next_gen1, gpu_compute_module_1_next_gen2,
       gpu_compute_module_1_next_gen3, gpu_compute_module_1_next_gen4, gpu_compute_module_1_next_gen5,
       gpu_compute_module_1_next_gen6, gpu_compute_module_1_next_gen7, gpu_compute_module_1_next_gen8,
       gpu_compute_module_1_next_gen9, gpu_compute_module_1_next_gen10, gpu_compute_module_1_next_gen11,
       gpu_compute_module_1_next_gen12, gpu_compute_module_1_next_gen13, gpu_compute_module_1_next_gen14,
       gpu_compute_module_1_next_gen15, gpu_compute_module_1_next_gen15_2, gpu_compute_module_1_next_gen17,
       gpu_compute_module_1_next_gen18, gpu_compute_module_1_next_gen19, gpu_compute_module_1_next_gen20,
       gpu_compute_module_1_next_gen21, gpu_compute_module_1_next_gen22, gpu_compute_module_1_next_gen23,
       gpu_compute_module_1_next_gen24, gpu_compute_module_1_next_gen25, gpu_compute_module_1_next_gen26,
       gpu_compute_module_1_next_gen27, gpu_compute_module_1_next_gen28, gpu_compute_module_1_next_gen29,
       gpu_compute_module_1_next_gen30, gpu_compute_module_1_next_gen31, gpu_str_mem_1_pos_next,
       gpu_str_mem_2_pos_next, gpu_str_mem_3_pos_next, gpu_str_mem_4_pos_next, gpu_str_mem_5_pos_next,
       gpu_str_mem_6_pos_next, gpu_str_mem_7_pos_next, gpu_str_mem_8_pos_next, gpu_str_mem_9_pos_next,
       gpu_str_mem_10_pos_next, gpu_str_mem_11_pos_next, gpu_str_mem_12_pos_next, gpu_str_mem_13_pos_next,
       gpu_str_mem_14_pos_next, gpu_str_mem_15_pos_next, gpu_str_mem_16_pos_next, gpu_str_mem_17_pos_next,
       gpu_str_mem_18_pos_next, gpu_str_mem_19_pos_next, gpu_str_mem_20_pos_next, gpu_str_mem_21_pos_next,
       gpu_str_mem_22_pos_next, gpu_str_mem_23_pos_next, gpu_str_mem_24_pos_next, gpu_str_mem_25_pos_next,
       gpu_str_mem_26_pos_next, gpu_str_mem_27_pos_next, gpu_str_mem_28_pos_next, gpu_str_mem_29_pos_next,
       gpu_str_mem_30_pos_next, gpu_str_mem_32_pos_next;

  gpu_str_mem gpu_str_mem_1 (
    .data(data), .addr(addr), .str(str0), .pos(start_pos), .clock(clock), .pos_next(gpu_str_mem_1_pos_next));
  gpu_str_mem gpu_str_mem_2 (
    .data(data), .addr(addr), .str(str1), .pos(gpu_str_mem_1_pos_next), .clock(clock),
    .pos_next(gpu_str_mem_2_pos_next));
  gpu_str_mem gpu_str_mem_3 (
    .data(data), .addr(addr), .str(str2), .pos(gpu_str_mem_2_pos_next), .clock(clock),
    .pos_next(gpu_str_mem_3_pos_next));
  gpu_str_mem gpu_str_mem_4 (
    .data(data), .addr(addr), .str(str3), .pos(gpu_str_mem_3_pos_next), .clock(clock),
    .pos_next(gpu_str_mem_4_pos_next));
  gpu_compute_module gpu_compute_module_1 (
    .str0(str0), .str1(str1), .str2(str2), .str3(str3), .str4(str4), .str5(str5), .str6(str6), .str7(str7),
    .str8(str8), .str9(str9), .str10(str10), .str11(str11), .str12(str12), .str13(str13), .str14(_14),
    .str15(str15), .str16(str0_2), .str17(str1_2), .str18(str2_2), .str19(str3_2), .str20(str4_2),
    .str21(str5_2), .str22(str6_2), .str23(str7_2), .str24(str8_2), .str25(str9_2), .str26(str10_2),
    .str27(str11_2), .str28(str12_2), .str29(str13_2), .str30(_14_2), .str31(str15_2),
    .str_right({18{1'b0}}), .str_left({18{1'b0}}), .str_up({32{1'b0}}), .str_down({32{1'b0}}),
    .next_gen0(gpu_compute_module_1_next_gen0), .next_gen1(gpu_compute_module_1_next_gen1),
    .next_gen2(gpu_compute_module_1_next_gen2), .next_gen3(gpu_compute_module_1_next_gen3),
    .next_gen4(gpu_compute_module_1_next_gen4), .next_gen5(gpu_compute_module_1_next_gen5),
    .next_gen6(gpu_compute_module_1_next_gen6), .next_gen7(gpu_compute_module_1_next_gen7),
    .next_gen8(gpu_compute_module_1_next_gen8), .next_gen9(gpu_compute_module_1_next_gen9),
    .next_gen10(gpu_compute_module_1_next_gen10), .next_gen11(gpu_compute_module_1_next_gen11),
    .next_gen12(gpu_compute_module_1_next_gen12), .next_gen13(gpu_compute_module_1_next_gen13),
    .next_gen14(gpu_compute_module_1_next_gen14), .next_gen15(gpu_compute_module_1_next_gen15),
    .next_gen15_2(gpu_compute_module_1_next_gen15_2), .next_gen17(gpu_compute_module_1_next_gen17),
    .next_gen18(gpu_compute_module_1_next_gen18), .next_gen19(gpu_compute_module_1_next_gen19),
    .next_gen20(gpu_compute_module_1_next_gen20), .next_gen21(gpu_compute_module_1_next_gen21),
    .next_gen22(gpu_compute_module_1_next_gen22), .next_gen23(gpu_compute_module_1_next_gen23),
    .next_gen24(gpu_compute_module_1_next_gen24), .next_gen25(gpu_compute_module_1_next_gen25),
    .next_gen26(gpu_compute_module_1_next_gen26), .next_gen27(gpu_compute_module_1_next_gen27),
    .next_gen28(gpu_compute_module_1_next_gen28), .next_gen29(gpu_compute_module_1_next_gen29),
    .next_gen30(gpu_compute_module_1_next_gen30), .next_gen31(gpu_compute_module_1_next_gen31));
  gpu_str_mem gpu_str_mem_5 (
    .data(data), .addr(addr), .str(str4), .pos(gpu_str_mem_4_pos_next), .clock(clock),
    .pos_next(gpu_str_mem_5_pos_next));
  gpu_str_mem gpu_str_mem_6 (
    .data(data), .addr(addr), .str(str5), .pos(gpu_str_mem_5_pos_next), .clock(clock),
    .pos_next(gpu_str_mem_6_pos_next));
  gpu_str_mem gpu_str_mem_7 (
    .data(data), .addr(addr), .str(str6), .pos(gpu_str_mem_6_pos_next), .clock(clock),
    .pos_next(gpu_str_mem_7_pos_next));
  gpu_str_mem gpu_str_mem_8 (
    .data(data), .addr(addr), .str(str7), .pos(gpu_str_mem_7_pos_next), .clock(clock),
    .pos_next(gpu_str_mem_8_pos_next));
  gpu_str_mem gpu_str_mem_9 (
    .data(data), .addr(addr), .str(str8), .pos(gpu_str_mem_8_pos_next), .clock(clock),
    .pos_next(gpu_str_mem_9_pos_next));
  gpu_str_mem gpu_str_mem_10 (
    .data(data), .addr(addr), .str(str11), .pos(gpu_str_mem_11_pos_next), .clock(clock),
    .pos_next(gpu_str_mem_10_pos_next));
  gpu_str_mem gpu_str_mem_11 (
    .data(data), .addr(addr), .str(str10), .pos(gpu_str_mem_12_pos_next), .clock(clock),
    .pos_next(gpu_str_mem_11_pos_next));
  gpu_str_mem gpu_str_mem_12 (
    .data(data), .addr(addr), .str(str9), .pos(gpu_str_mem_9_pos_next), .clock(clock),
    .pos_next(gpu_str_mem_12_pos_next));
  DotMatrix #(.matrixcols(32), .matrixrows(16)) dotmatrix_1 (
    .col0(gpu_compute_module_1_next_gen0), .col1(gpu_compute_module_1_next_gen1),
    .col2(gpu_compute_module_1_next_gen2), .col3(gpu_compute_module_1_next_gen3),
    .col4(gpu_compute_module_1_next_gen4), .col5(gpu_compute_module_1_next_gen5),
    .col6(gpu_compute_module_1_next_gen6), .col7(gpu_compute_module_1_next_gen7),
    .col8(gpu_compute_module_1_next_gen8), .col9(gpu_compute_module_1_next_gen9),
    .col10(gpu_compute_module_1_next_gen10), .col11(gpu_compute_module_1_next_gen11),
    .col12(gpu_compute_module_1_next_gen12), .col13(gpu_compute_module_1_next_gen13),
    .col14(gpu_compute_module_1_next_gen14), .col15(gpu_compute_module_1_next_gen15),
    .col16(gpu_compute_module_1_next_gen15_2), .col17(gpu_compute_module_1_next_gen17),
    .col18(gpu_compute_module_1_next_gen18), .col19(gpu_compute_module_1_next_gen19),
    .col20(gpu_compute_module_1_next_gen20), .col21(gpu_compute_module_1_next_gen21),
    .col22(gpu_compute_module_1_next_gen22), .col23(gpu_compute_module_1_next_gen23),
    .col24(gpu_compute_module_1_next_gen24), .col25(gpu_compute_module_1_next_gen25),
    .col26(gpu_compute_module_1_next_gen26), .col27(gpu_compute_module_1_next_gen27),
    .col28(gpu_compute_module_1_next_gen28), .col29(gpu_compute_module_1_next_gen29),
    .col30(gpu_compute_module_1_next_gen30), .col31(gpu_compute_module_1_next_gen31));
  gpu_str_mem gpu_str_mem_13 (
    .data(data), .addr(addr), .str(str12), .pos(gpu_str_mem_10_pos_next), .clock(clock),
    .pos_next(gpu_str_mem_13_pos_next));
  gpu_str_mem gpu_str_mem_14 (
    .data(data), .addr(addr), .str(str13), .pos(gpu_str_mem_13_pos_next), .clock(clock),
    .pos_next(gpu_str_mem_14_pos_next));
  gpu_str_mem gpu_str_mem_15 (
    .data(data), .addr(addr), .str(_14), .pos(gpu_str_mem_14_pos_next), .clock(clock),
    .pos_next(gpu_str_mem_15_pos_next));
  gpu_str_mem gpu_str_mem_16 (
    .data(data), .addr(addr), .str(str15), .pos(gpu_str_mem_15_pos_next), .clock(clock),
    .pos_next(gpu_str_mem_16_pos_next));
  gpu_str_mem gpu_str_mem_17 (
    .data(data), .addr(addr), .str(str0_2), .pos(gpu_str_mem_16_pos_next), .clock(clock),
    .pos_next(gpu_str_mem_17_pos_next));
  gpu_str_mem gpu_str_mem_18 (
    .data(data), .addr(addr), .str(str3_2), .pos(gpu_str_mem_20_pos_next), .clock(clock),
    .pos_next(gpu_str_mem_18_pos_next));
  gpu_str_mem gpu_str_mem_19 (
    .data(data), .addr(addr), .str(str1_2), .pos(gpu_str_mem_17_pos_next), .clock(clock),
    .pos_next(gpu_str_mem_19_pos_next));
  gpu_str_mem gpu_str_mem_20 (
    .data(data), .addr(addr), .str(str2_2), .pos(gpu_str_mem_19_pos_next), .clock(clock),
    .pos_next(gpu_str_mem_20_pos_next));
  gpu_str_mem gpu_str_mem_21 (
    .data(data), .addr(addr), .str(str5_2), .pos(gpu_str_mem_22_pos_next), .clock(clock),
    .pos_next(gpu_str_mem_21_pos_next));
  gpu_str_mem gpu_str_mem_22 (
    .data(data), .addr(addr), .str(str4_2), .pos(gpu_str_mem_18_pos_next), .clock(clock),
    .pos_next(gpu_str_mem_22_pos_next));
  gpu_str_mem gpu_str_mem_23 (
    .data(data), .addr(addr), .str(str6_2), .pos(gpu_str_mem_21_pos_next), .clock(clock),
    .pos_next(gpu_str_mem_23_pos_next));
  gpu_str_mem gpu_str_mem_24 (
    .data(data), .addr(addr), .str(str8_2), .pos(gpu_str_mem_25_pos_next), .clock(clock),
    .pos_next(gpu_str_mem_24_pos_next));
  gpu_str_mem gpu_str_mem_25 (
    .data(data), .addr(addr), .str(str7_2), .pos(gpu_str_mem_23_pos_next), .clock(clock),
    .pos_next(gpu_str_mem_25_pos_next));
  gpu_str_mem gpu_str_mem_26 (
    .data(data), .addr(addr), .str(str9_2), .pos(gpu_str_mem_24_pos_next), .clock(clock),
    .pos_next(gpu_str_mem_26_pos_next));
  gpu_str_mem gpu_str_mem_27 (
    .data(data), .addr(addr), .str(str11_2), .pos(gpu_str_mem_28_pos_next), .clock(clock),
    .pos_next(gpu_str_mem_27_pos_next));
  gpu_str_mem gpu_str_mem_28 (
    .data(data), .addr(addr), .str(str10_2), .pos(gpu_str_mem_26_pos_next), .clock(clock),
    .pos_next(gpu_str_mem_28_pos_next));
  gpu_str_mem gpu_str_mem_29 (
    .data(data), .addr(addr), .str(str13_2), .pos(gpu_str_mem_30_pos_next), .clock(clock),
    .pos_next(gpu_str_mem_29_pos_next));
  gpu_str_mem gpu_str_mem_30 (
    .data(data), .addr(addr), .str(str12_2), .pos(gpu_str_mem_27_pos_next), .clock(clock),
    .pos_next(gpu_str_mem_30_pos_next));
  gpu_str_mem gpu_str_mem_31 (
    .data(data), .addr(addr), .str(str15_2), .pos(gpu_str_mem_32_pos_next), .clock(clock), .pos_next(next_pos));
  gpu_str_mem gpu_str_mem_32 (
    .data(data), .addr(addr), .str(_14_2), .pos(gpu_str_mem_29_pos_next), .clock(clock),
    .pos_next(gpu_str_mem_32_pos_next));

  assign addr_pass = addr;
  assign clock_out = clock;
  assign data_pass = data;

  // Other names for the same wires on the sheet: str14[15:0] = _14; str16[15:0] = str0_2; str17[15:0] = str1_2;
  //   str18[15:0] = str2_2; str19[15:0] = str3_2; str20[15:0] = str4_2; str21[15:0] = str5_2; str22[15:0] = str6_2;
  //   str23[15:0] = str7_2; str24[15:0] = str8_2; str25[15:0] = str9_2; str26[15:0] = str10_2; str27[15:0] = str11_2;
  //   str28[15:0] = str12_2; str29[15:0] = str13_2; str30[15:0] = _14_2; str31[15:0] = str15_2
endmodule

// CU
module cu (
  input  \cell ,
  input  [7:0] neighbors,
  output new_gen
);

  wire comparator_1_eq, comparator_2_eq, or_1_out;
  wire [3:0] bitadder_1_out;

  BitAdder bitadder_1 (.in0(neighbors), .out(bitadder_1_out));
  Comparator #(.width(4), .mode("unsigned")) comparator_1 (
    .a(bitadder_1_out), .b(4'b0011), .eq(comparator_1_eq));  // open: gt, lt
  Comparator #(.width(4), .mode("unsigned")) comparator_2 (
    .a(bitadder_1_out), .b(4'b0010), .eq(comparator_2_eq));  // open: gt, lt
  or or_1 (or_1_out, comparator_1_eq, comparator_2_eq);
  Multiplexer multiplexer_1 (.in0(comparator_1_eq), .in1(or_1_out), .out(new_gen), .sel(\cell ));  // open: en
endmodule

// COMPUTE\nUNITS
module cu_block (
  input  [15:0] left_row,
  input  [15:0] center_row,
  input  [15:0] right_row,
  input  [5:0] cycle,
  output [15:0] computed_row
);

  cu _15 (
    .\cell (center_row[15]),
    .neighbors({cycle[4:3], right_row[15:14], center_row[14], left_row[14], left_row[15], cycle[5]}),
    .new_gen(computed_row[15]));
  cu _14 (
    .\cell (center_row[14]),
    .neighbors({center_row[15], right_row[15:13], center_row[13], left_row[13], left_row[14], left_row[15]}),
    .new_gen(computed_row[14]));
  cu _13 (
    .\cell (center_row[13]),
    .neighbors({center_row[14], right_row[14:12], center_row[12], left_row[12], left_row[13], left_row[14]}),
    .new_gen(computed_row[13]));
  cu _12 (
    .\cell (center_row[12]),
    .neighbors({center_row[13], right_row[13:11], center_row[11], left_row[11], left_row[12], left_row[13]}),
    .new_gen(computed_row[12]));
  cu _11 (
    .\cell (center_row[11]),
    .neighbors({center_row[12], right_row[12:10], center_row[10], left_row[10], left_row[11], left_row[12]}),
    .new_gen(computed_row[11]));
  cu _10 (
    .\cell (center_row[10]),
    .neighbors({center_row[11], right_row[11:9], center_row[9], left_row[9], left_row[10], left_row[11]}),
    .new_gen(computed_row[10]));
  cu _9 (
    .\cell (center_row[9]),
    .neighbors({center_row[10], right_row[10:8], center_row[8], left_row[8], left_row[9], left_row[10]}),
    .new_gen(computed_row[9]));
  cu _8 (
    .\cell (center_row[8]),
    .neighbors({center_row[9], right_row[9:7], center_row[7], left_row[7], left_row[8], left_row[9]}),
    .new_gen(computed_row[8]));
  cu _7 (
    .\cell (center_row[7]),
    .neighbors({center_row[8], right_row[8:6], center_row[6], left_row[6], left_row[7], left_row[8]}),
    .new_gen(computed_row[7]));
  cu _6 (
    .\cell (center_row[6]),
    .neighbors({center_row[7], right_row[7:5], center_row[5], left_row[5], left_row[6], left_row[7]}),
    .new_gen(computed_row[6]));
  cu _5 (
    .\cell (center_row[5]),
    .neighbors({center_row[6], right_row[6:4], center_row[4], left_row[4], left_row[5], left_row[6]}),
    .new_gen(computed_row[5]));
  cu _4 (
    .\cell (center_row[4]),
    .neighbors({center_row[5], right_row[5:3], center_row[3], left_row[3], left_row[4], left_row[5]}),
    .new_gen(computed_row[4]));
  cu _3 (
    .\cell (center_row[3]),
    .neighbors({center_row[4], right_row[4:2], center_row[2], left_row[2], left_row[3], left_row[4]}),
    .new_gen(computed_row[3]));
  cu _2 (
    .\cell (center_row[2]),
    .neighbors({center_row[3], right_row[3:1], center_row[1], left_row[1], left_row[2], left_row[3]}),
    .new_gen(computed_row[2]));
  cu _1 (
    .\cell (center_row[1]),
    .neighbors({center_row[2], right_row[2:0], center_row[1], left_row[0], left_row[1], left_row[2]}),
    .new_gen(computed_row[1]));
  cu _0 (
    .\cell (center_row[0]),
    .neighbors({center_row[1], right_row[1:0], cycle[0], cycle[1], cycle[2], left_row[0], left_row[1]}),
    .new_gen(computed_row[0]));
endmodule

// GPU\nCOMPUTE MODULE
module gpu_compute_module (
  input  [15:0] str0,
  input  [15:0] str1,
  input  [15:0] str2,
  input  [15:0] str3,
  input  [15:0] str4,
  input  [15:0] str5,
  input  [15:0] str6,
  input  [15:0] str7,
  input  [15:0] str8,
  input  [15:0] str9,
  input  [15:0] str10,
  input  [15:0] str11,
  input  [15:0] str12,
  input  [15:0] str13,
  input  [15:0] str14,
  input  [15:0] str15,
  input  [15:0] str16,
  input  [15:0] str17,
  input  [15:0] str18,
  input  [15:0] str19,
  input  [15:0] str20,
  input  [15:0] str21,
  input  [15:0] str22,
  input  [15:0] str23,
  input  [15:0] str24,
  input  [15:0] str25,
  input  [15:0] str26,
  input  [15:0] str27,
  input  [15:0] str28,
  input  [15:0] str29,
  input  [15:0] str30,
  input  [15:0] str31,
  input  [17:0] str_right,
  input  [17:0] str_left,
  input  [31:0] str_up,
  input  [31:0] str_down,
  output [15:0] next_gen0,
  output [15:0] next_gen1,
  output [15:0] next_gen2,
  output [15:0] next_gen3,
  output [15:0] next_gen4,
  output [15:0] next_gen5,
  output [15:0] next_gen6,
  output [15:0] next_gen7,
  output [15:0] next_gen8,
  output [15:0] next_gen9,
  output [15:0] next_gen10,
  output [15:0] next_gen11,
  output [15:0] next_gen12,
  output [15:0] next_gen13,
  output [15:0] next_gen14,
  output [15:0] next_gen15,
  output [15:0] next_gen15_2,
  output [15:0] next_gen17,
  output [15:0] next_gen18,
  output [15:0] next_gen19,
  output [15:0] next_gen20,
  output [15:0] next_gen21,
  output [15:0] next_gen22,
  output [15:0] next_gen23,
  output [15:0] next_gen24,
  output [15:0] next_gen25,
  output [15:0] next_gen26,
  output [15:0] next_gen27,
  output [15:0] next_gen28,
  output [15:0] next_gen29,
  output [15:0] next_gen30,
  output [15:0] next_gen31
);

  cu_block _0 (
    .left_row(str_left[16:1]), .center_row(str0), .right_row(str1),
    .cycle({str_left[17], str_up[1:0], str_left[0], str_down[1:0]}), .computed_row(next_gen0));
  cu_block _1 (
    .left_row(str0), .center_row(str1), .right_row(str2), .cycle({str_up[2:0], str_down[2:0]}),
    .computed_row(next_gen1));
  cu_block _2 (
    .left_row(str1), .center_row(str2), .right_row(str3), .cycle({str_up[3:1], str_down[3:1]}),
    .computed_row(next_gen2));
  cu_block _3 (
    .left_row(str2), .center_row(str3), .right_row(str4), .cycle({str_up[4:2], str_down[4:2]}),
    .computed_row(next_gen3));
  cu_block _4 (
    .left_row(str3), .center_row(str4), .right_row(str5), .cycle({str_up[5:3], str_down[5:3]}),
    .computed_row(next_gen4));
  cu_block _5 (
    .left_row(str4), .center_row(str5), .right_row(str6), .cycle({str_up[6:4], str_down[6:4]}),
    .computed_row(next_gen5));
  cu_block _6 (
    .left_row(str5), .center_row(str6), .right_row(str7), .cycle({str_up[7:5], str_down[7:5]}),
    .computed_row(next_gen6));
  cu_block _8 (
    .left_row(str7), .center_row(str8), .right_row(str9), .cycle({str_up[9:7], str_down[9:7]}),
    .computed_row(next_gen8));
  cu_block _7 (
    .left_row(str6), .center_row(str7), .right_row(str8), .cycle({str_up[8:6], str_down[8:6]}),
    .computed_row(next_gen7));
  cu_block _9 (
    .left_row(str8), .center_row(str9), .right_row(str10), .cycle({str_up[10:8], str_down[10:8]}),
    .computed_row(next_gen9));
  cu_block _10 (
    .left_row(str9), .center_row(str10), .right_row(str11), .cycle({str_up[11:9], str_down[11:9]}),
    .computed_row(next_gen10));
  cu_block _11 (
    .left_row(str10), .center_row(str11), .right_row(str12), .cycle({str_up[12:10], str_down[12:10]}),
    .computed_row(next_gen11));
  cu_block _12 (
    .left_row(str11), .center_row(str12), .right_row(str13), .cycle({str_up[13:11], str_down[13:11]}),
    .computed_row(next_gen12));
  cu_block _13 (
    .left_row(str12), .center_row(str13), .right_row(str14), .cycle({str_up[14:12], str_down[14:12]}),
    .computed_row(next_gen13));
  cu_block _14 (
    .left_row(str13), .center_row(str14), .right_row(str15), .cycle({str_up[15:13], str_down[15:13]}),
    .computed_row(next_gen14));
  cu_block _16 (
    .left_row(str15), .center_row(str16), .right_row(str17), .cycle({str_up[17:15], str_down[17:15]}),
    .computed_row(next_gen15_2));
  cu_block _15 (
    .left_row(str14), .center_row(str15), .right_row(str16), .cycle({str_up[16:14], str_down[16:14]}),
    .computed_row(next_gen15));
  cu_block _17 (
    .left_row(str16), .center_row(str17), .right_row(str18), .cycle({str_up[18:16], str_down[18:16]}),
    .computed_row(next_gen17));
  cu_block _18 (
    .left_row(str17), .center_row(str18), .right_row(str19), .cycle({str_up[19:17], str_down[19:17]}),
    .computed_row(next_gen18));
  cu_block _19 (
    .left_row(str18), .center_row(str19), .right_row(str20), .cycle({str_up[20:18], str_down[20:18]}),
    .computed_row(next_gen19));
  cu_block _20 (
    .left_row(str19), .center_row(str20), .right_row(str21), .cycle({str_up[21:19], str_down[21:19]}),
    .computed_row(next_gen20));
  cu_block _21 (
    .left_row(str20), .center_row(str21), .right_row(str22), .cycle({str_up[22:20], str_down[22:20]}),
    .computed_row(next_gen21));
  cu_block _22 (
    .left_row(str21), .center_row(str22), .right_row(str23), .cycle({str_up[23:21], str_down[23:21]}),
    .computed_row(next_gen22));
  cu_block _24 (
    .left_row(str23), .center_row(str24), .right_row(str25), .cycle({str_up[25:23], str_down[25:23]}),
    .computed_row(next_gen24));
  cu_block _23 (
    .left_row(str22), .center_row(str23), .right_row(str24), .cycle({str_up[24:22], str_down[24:22]}),
    .computed_row(next_gen23));
  cu_block _25 (
    .left_row(str24), .center_row(str25), .right_row(str26), .cycle({str_up[26:24], str_down[26:24]}),
    .computed_row(next_gen25));
  cu_block _26 (
    .left_row(str25), .center_row(str26), .right_row(str27), .cycle({str_up[27:25], str_down[27:25]}),
    .computed_row(next_gen26));
  cu_block _27 (
    .left_row(str26), .center_row(str27), .right_row(str28), .cycle({str_up[28:26], str_down[28:26]}),
    .computed_row(next_gen27));
  cu_block _28 (
    .left_row(str27), .center_row(str28), .right_row(str29), .cycle({str_up[29:27], str_down[29:27]}),
    .computed_row(next_gen28));
  cu_block _29 (
    .left_row(str28), .center_row(str29), .right_row(str30), .cycle({str_up[30:28], str_down[30:28]}),
    .computed_row(next_gen29));
  cu_block _30 (
    .left_row(str29), .center_row(str30), .right_row(str31), .cycle({str_up[31:29], str_down[31:29]}),
    .computed_row(next_gen30));
  cu_block _31 (
    .left_row(str30), .center_row(str31), .right_row(str_right[16:1]),
    .cycle({str_right[17], str_up[31:30], str_right[0], str_down[31:30]}), .computed_row(next_gen31));
endmodule
